# Fritzing sketch 回路図 (saved by Fritzing 0.9.5d)
breadboards: 1

parts:
  パーツ1 = Arduino Uno (Rev3)
  S2 = SWITCH-MOMENTARY-2 [package=tactile-pth-12mm]
  S3 = SWITCH-MOMENTARY-2 [package=tactile-pth-12mm]
  r2 = Resistor [tolerance=±5% resistance=10k package=THT]
  R3 = Resistor [tolerance=±5% resistance=10k package=THT]
  R4 = Resistor [tolerance=±5% resistance=10k package=THT]
  R5 = Resistor [tolerance=±5% resistance=10k package=THT]
  R6 = Resistor [tolerance=±5% resistance=10k package=THT]
  SP1 = SPEAKER [package=pcb_mount_speaker]
  C1 = Electrolytic Capacitor [capacitance=4.7µF package="100 mil [THT, electrolytic]"]
  L_limirt = Round Pushbutton
  R_limit = Round Pushbutton
  sens = Round Pushbutton
  C3 = Ceramic Capacitor [capacitance=100nF package="100 mil [THT, multilayer]"]
  C4 = Ceramic Capacitor [capacitance=100nF package="100 mil [THT, multilayer]"]
  C5 = Ceramic Capacitor [capacitance=100nF package="100 mil [THT, multilayer]"]
  C6 = Ceramic Capacitor [capacitance=100nF package="100 mil [THT, multilayer]"]
  C7 = Ceramic Capacitor [capacitance=100nF package="100 mil [THT, multilayer]"]
  U1 = LM386 [package=dip08]
  C8 = Electrolytic Capacitor [capacitance=4.7µF package="100 mil [THT, electrolytic]"]
  R7 = Resistor [tolerance=±5% resistance=100k package=THT]
  VCC1 = Battery block 9V
  C9 = Electrolytic Capacitor [capacitance=4.7µF package="100 mil [THT, electrolytic]"]
  LED1 = LEDs [package=led-0603]
  R8 = Resistor [tolerance=±5% resistance=10k package=THT]

nets:
  N1: パーツ1.D8, R4.Pin_0, L_limirt.leg1, C7.1
  N2: パーツ1.D9_PWM, R6.Pin_0, R_limit.leg1, C5.1
  N3: パーツ1.D10_PWM/SS, R5.Pin_0, sens.leg1, C6.1
  N4: パーツ1.D12/MISO, R8.Pin_1
  N5: パーツ1.D13/SCK, C1.+
  N6: パーツ1.GND, r2.Pin_1, R3.Pin_1, SP1.-, L_limirt.leg0, R_limit.leg0, sens.leg0, C3.1, C4.1, C5.0, C6.0, C7.0, U1.-IN, U1.V-, R7.Pin_0, VCC1.-, C9.-, LED1.C
  N7: パーツ1.D5_PWM, S2.1, r2.Pin_0, C3.0
  N8: パーツ1.D6_PWM, S3.1, R3.Pin_0, C4.0
  N9: パーツ1.5V, S2.2, S3.2, R4.Pin_1, R5.Pin_1, R6.Pin_1
  N10: SP1.+, C8.-
  N11: C1.-, U1.+IN, R7.Pin_1
  N12: U1.OUT, C8.+
  N13: U1.V+, VCC1.+
  N14: U1.BP, C9.+
  N15: LED1.A, R8.Pin_0
